# Fritzing sketch rainSensor (saved by Fritzing 0.9.3b)
circuit board: 8.46667cm x 5.64444cm
breadboards: 1

parts:
  YL-83_-_Detection_Board1 = YL-83 Rain Sensor - Detection Board
  YL-83_-_Control_Board1 = YL-83 Rain Sensor - Control Board
  Mod1 = Raspberry Pi Pico
  Part1 = LCD1602-I2C

nets:
  N1: YL-83_-_Detection_Board1.POS, YL-83_-_Control_Board1.POS
  N2: YL-83_-_Detection_Board1.NEG, YL-83_-_Control_Board1.NEG
  VCC: YL-83_-_Control_Board1.VCC, Mod1.pin_40, Part1.VCC
  GND: YL-83_-_Control_Board1.GND, YL-83_-_Control_Board1.DO, Mod1.pin_3, Mod1.pin_8, Mod1.pin_13, Mod1.pin_18, Mod1.pin_23, Mod1.pin_28, Mod1.pin_33, Mod1.pin_38, Part1.GND
  N3: YL-83_-_Control_Board1.AO, Mod1.pin_31
  N4: Mod1.pin_1, Part1.SDA
  N5: Mod1.pin_2, Part1.SCL

custom parts:
  YL-83 Rain Sensor - Detection Board: The YL-83 is a rain sensor that has more resistance when dry and less resistance when wet. The module runs at 5V.
  YL-83 Rain Sensor - Control Board: The YL-83 is a rain sensor that has more resistance when dry and less resistance when wet. The module runs at 5V.
  Raspberry Pi Pico: Raspberry Pi Pico. Based around the RP2040 microcontroller the Pico is a low cost microcontroller device bringing Raspberry Pi quality, cost, and easy of use to the microcontroller space. Jan 2021, Split part in to two versions: tht (this one) and SMD. This one will drill holes for a .1 in header in pcb to allow plugging in the module as well as providing pads to solder the module to the top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
  LCD1602-I2C: A standard character display, usually with 2x16 characters. Comes in many colors with LCM1602 IIC attached.
